# Fritzing sketch avoider (saved by Fritzing 0.9.3b)
breadboards: 1

parts:
  Motor_controller1 = L298 [package=multiwatt15_6400bgheatsink]
  Raspberry_Pi_1 = Raspberry Pi 3 [part_number=RPI-3-V1.2]
  IR3 = TSOP312.., 314.. [package=THT]
  IR4 = TSOP312.., 314.. [package=THT]
  UltraSonic_Sensor = hc-sr04
  ultraonic_sensor_servo1 = Basic Servo
  R4 = Resistor [tolerance=±5% resistance=1k package=THT]
  R5 = Resistor [tolerance=±5% resistance=2k package=THT]
  M5 = DC Motor
  M6 = DC Motor
  BAT2 = Battery Holders [package=battery-aa]

nets:
  N1: Motor_controller1.OUT1, M5.pin_1
  N2: Motor_controller1.OUT2, M5.pin_2
  N3: Motor_controller1.IN1, Raspberry_Pi_1.GIPO6
  N4: Motor_controller1.IN2, Raspberry_Pi_1.GIPO13
  N5: Motor_controller1.GND, BAT2.-
  N6: Motor_controller1.VLS, BAT2.+
  N7: Motor_controller1.IN3, Raspberry_Pi_1.GIPO19
  N8: Motor_controller1.IN4, Raspberry_Pi_1.GIPO26
  N9: Motor_controller1.OUT3, M6.pin_1
  N10: Motor_controller1.OUT4, M6.pin_2
  N11: Raspberry_Pi_1.GIPO4, Raspberry_Pi_1.5V, UltraSonic_Sensor.Trig
  N12: Raspberry_Pi_1.GIPO10, ultraonic_sensor_servo1.pulse
  N13: Raspberry_Pi_1.GIPO7, IR4.Data
  N14: Raspberry_Pi_1.GIPO8, IR3.Data
  N15: Raspberry_Pi_1.GIPO18, R4.Pin_1, R5.Pin_0
  N16: UltraSonic_Sensor.Echo, R4.Pin_0

notes:
  Raspberry Pi Project
  Obstacle Avoidance Robot
  November, 2016
  5V
  3.3V
