# Fritzing sketch obstacle_avoiding_robot (saved by Fritzing 0.9.3b)
breadboards: 1

parts:
  M3 = DC Motor
  M4 = DC Motor
  Ultrasonic_sensor1 = hc-sr04
  R1 = Resistor [tolerance=±5% resistance=680 package=THT]
  R2 = Resistor [tolerance=±5% resistance=1k package=THT]
  Raspberry_Pi_B_rev1 = Raspberry Pi B rev1
  Motor_controller = L298 [package=multiwatt15_6400bgheatsink]
  BAT1 = Battery Holders [package=battery-aa]

nets:
  N1: M3.pin_1, Motor_controller.OUT1
  N2: M3.pin_2, Motor_controller.OUT2
  N3: M4.pin_1, Motor_controller.OUT3
  N4: M4.pin_2, Motor_controller.OUT4
  GND: Ultrasonic_sensor1.Trig, Raspberry_Pi_B_rev1.5V, Raspberry_Pi_B_rev1.GPIO_24
  N5: Ultrasonic_sensor1.Echo, R1.Pin_0
  GND_2: Ultrasonic_sensor1.GND, R2.Pin_0, Raspberry_Pi_B_rev1.GND
  N6: R1.Pin_1, R2.Pin_1, Raspberry_Pi_B_rev1.GPIO_23
  N7: Raspberry_Pi_B_rev1.GPIO_17, Motor_controller.IN2
  N8: Raspberry_Pi_B_rev1.GPIO_21, Motor_controller.IN3
  N9: Raspberry_Pi_B_rev1.GPIO_22, Motor_controller.IN4
  N10: Raspberry_Pi_B_rev1.GPIO_4, Motor_controller.IN1
  N11: Motor_controller.GND, BAT1.-
  N12: Motor_controller.VLS, BAT1.+

notes:
  Raspberry Pi Project
  Obstacle Avoidance Robot
  Sept, 2016
  5V
  3.3V
